# Fritzing sketch sketch (saved by Fritzing 0.9.3b)

parts:
  Part1 = Adafruit Trinket M0 [part_number="Adafruit #3500"]
  J1 = Piezo Speaker

nets:
  N1: Part1.GND, J1.pin2
  N2: Part1.D3_A3_PA07_RXD_SCK, J1.pin1
